# Fritzing sketch Motor_Driver_Board_TLE4202B (saved by Fritzing 0.9.3b)
circuit board: 2.57031cm x 3.10711cm

parts:
  TLE4202B = mystery part, 8 pins [chip_label=TLE4202B]
  Input = mystery part, 6 pins [chip_label=?]
  Motor_out = Screw terminal - 2 pins [package=THT]
  Solenoid_out = Screw terminal - 2 pins [package=THT]
  Q1 = Basic FET N-Channel [package="TO220 [THT]"]
  D1 = Rectifier Diode [part_number=1N4001 package="300 mil [THT]"]
  R1 = Resistor [tolerance=±5% resistance=10k package=THT]
  R2 = Resistor [tolerance=±5% resistance=220 package=THT]
  R3 = Resistor [tolerance=±5% resistance=10k package=THT]
  R4 = Resistor [tolerance=±5% resistance=10k package=THT]

nets:
  GND: TLE4202B.pin3, Input.pin3, Q1.source, R1.Pin_1, R3.Pin_1, R4.Pin_1
  12V: TLE4202B.pin4, Input.pin4, Solenoid_out.pin2, D1.cathode
  N1: TLE4202B.pin5, Input.pin2, R4.Pin_0
  N2: TLE4202B.pin6, Motor_out.pin1
  N3: TLE4202B.pin7, Motor_out.pin2
  N4: TLE4202B.pin8, Input.pin1, R3.Pin_0
  N5: Input.pin6, R2.Pin_0
  N6: Solenoid_out.pin1, Q1.drain, D1.anode
  N7: Q1.gate, R1.Pin_0, R2.Pin_1
