# Fritzing sketch chicken_stall_door_schematic (saved by Fritzing 0.9.3b)
circuit board: 4.25691cm x 7.45591cm

parts:
  Door_Motor = DC Motor
  Main_12V_in = Screw terminal - 2 pins [package=THT]
  Limitswitch_Top = Reed switch [package=THT]
  Limitswitch_Bottom = Reed switch [package=THT]
  Error = LED - 5mm [color="Red (633nm)" package="5 mm [THT]"]
  Powerswitch = Round Pushbutton
  Up = Round Pushbutton
  Down = Round Pushbutton
  Arduino_Nano = Arduino Nano (Rev3.0)
  LM7805 = Voltage Regulator [package=to220-igo]
  Stop = Round Pushbutton
  Motor = LED - 5mm [color="Yellow (595nm)" package="5 mm [THT]"]
  Power = LED - 5mm [color="Green (560nm)" package="5 mm [THT]"]
  R1 = Resistor [tolerance=±5% resistance=220 package=THT]
  R2 = Resistor [tolerance=±5% resistance=220 package=THT]
  R3 = Resistor [tolerance=±5% resistance=220 package=THT]
  C1 = Electrolytic Capacitor [capacitance=10µF voltage=16V package="200 mil [THT, electrolytic]"]
  UART = male pin header, 3 pins [form="♂ (male)"]
  Front_out = male pin header, 7 pins [form="♂ (male)"]
  Limitswitch_out = screw terminal, 4 pins
  U2 = L9110 H-bridge module [part_number="L9110 H-bridge"]
  U3 = RF-LINK_RX [package=rf-link_rx]
  ANT1 = Antenna
  End-Stop_Emergency_(N_C_) = Round Pushbutton
  EndS_out = Screw terminal - 2 pins [package=THT]
  Solenoid_Lock = Solenoid
  H-Bridge_out = female pin header, 5 pins [form="♀ (female)"]
  D1 = Rectifier Diode [part_number=1N4001 package="300 mil [THT]"]
  PCB_Vin = Screw terminal - 2 pins [package=THT]

nets:
  N1: Door_Motor.pin_1, U2.MOTOR_A-A
  N2: Door_Motor.pin_2, U2.MOTOR_A-B
  GND: Main_12V_in.pin1, Limitswitch_Top.pin_1, Limitswitch_Bottom.pin_1, Error.cathode, Up.leg1, Down.leg1, Arduino_Nano.GND, LM7805.GND, Stop.leg1, Motor.cathode, Power.cathode, C1.-, UART.pin1, Front_out.pin7, Limitswitch_out.pin1, Limitswitch_out.pin4, U2.B-IB, U2.GND, U3.GND, H-Bridge_out.pin4, PCB_Vin.pin1
  N3: Main_12V_in.pin2, Powerswitch.leg0
  N4: Limitswitch_Top.pin_2, Arduino_Nano.A1, Limitswitch_out.pin2
  N5: Limitswitch_Bottom.pin_2, Arduino_Nano.A2, Limitswitch_out.pin3
  N6: Error.anode, R1.Pin_1, Front_out.pin4
  N7: Powerswitch.leg1, End-Stop_Emergency_(N_C_).leg0, EndS_out.pin1, PCB_Vin.pin2
  N8: Up.leg0, Arduino_Nano.D11/MOSI, Front_out.pin2
  N9: Down.leg0, Arduino_Nano.D12/MISO, Front_out.pin1
  N10: Arduino_Nano.D1/TX, UART.pin2
  N11: Arduino_Nano.D0/RX, UART.pin3
  N12: Arduino_Nano.D2, U3.DATA
  N13: Arduino_Nano.D4, U2.B-IA, H-Bridge_out.pin3
  N14: Arduino_Nano.D5, U2.A-IB, H-Bridge_out.pin2
  N15: Arduino_Nano.D6, U2.A-IA, H-Bridge_out.pin1
  N16: Arduino_Nano.D7, R3.Pin_0
  N17: Arduino_Nano.D8, R2.Pin_0
  N18: Arduino_Nano.D9, R1.Pin_0
  N19: Arduino_Nano.D10, Stop.leg0, Front_out.pin3
  5V: Arduino_Nano.5V, LM7805.OUT, C1.+, U3.+5V
  12V: LM7805.IN, U2.VCC, H-Bridge_out.pin5, D1.cathode
  N20: Motor.anode, R2.Pin_1, Front_out.pin5
  N21: Power.anode, R3.Pin_1, Front_out.pin6
  N22: U2.MOTOR_B-A, Solenoid_Lock.pin1
  N23: U2.MOTOR_B-B, Solenoid_Lock.pin2
  N24: U3.ANT, ANT1.antenna_lead
  N25: End-Stop_Emergency_(N_C_).leg1, EndS_out.pin2, D1.anode

notes:
  chicken stall door controller, 1.0
  Reverse Polarity Protection

custom parts:
  Round Pushbutton: A generic pushbutton.
